// Logisim project CPU.circ as structural Verilog: 33 circuits, main circuit One_Bit_Full_Adder
// ADD
module One_Bit_Full_Adder (
  input  A,
  input  B,
  input  C_IN,
  output SUM,
  output C_OUT
);

  wire and_1_out, and_2_out, xor_1_out;

  xor xor_1 (xor_1_out, A, B);
  xor xor_2 (SUM, xor_1_out, C_IN);
  and and_1 (and_1_out, C_IN, xor_1_out);
  and and_2 (and_2_out, B, A);
  or or_1 (C_OUT, and_1_out, and_2_out);
endmodule

// FOUR BIT FULL ADDER
module Four_Bit_Full_Adder_74LS283 (
  input  C_IN,
  input  A0,
  input  B0,
  input  A1,
  input  B1,
  input  A2,
  input  B2,
  input  A3,
  input  B3,
  output S0,
  output S1,
  output S2,
  output S3,
  output C_OUT
);

  wire one_bit_full_adder_1_c_out, one_bit_full_adder_2_c_out, one_bit_full_adder_3_c_out;

  One_Bit_Full_Adder one_bit_full_adder_1 (.A(A0), .B(B0), .C_IN(C_IN), .SUM(S0), .C_OUT(one_bit_full_adder_1_c_out));
  One_Bit_Full_Adder one_bit_full_adder_2 (
    .A(A1), .B(B1), .C_IN(one_bit_full_adder_1_c_out), .SUM(S1), .C_OUT(one_bit_full_adder_2_c_out));
  One_Bit_Full_Adder one_bit_full_adder_3 (
    .A(A2), .B(B2), .C_IN(one_bit_full_adder_2_c_out), .SUM(S2), .C_OUT(one_bit_full_adder_3_c_out));
  One_Bit_Full_Adder one_bit_full_adder_4 (.A(A3), .B(B3), .C_IN(one_bit_full_adder_3_c_out), .SUM(S3), .C_OUT(C_OUT));
endmodule

// FULL ADDER
module Eight_Bit_Full_Adder_2x74LS283 (
  input  C_IN,
  input  A0,
  input  B0,
  input  A1,
  input  B1,
  input  A2,
  input  B2,
  input  A3,
  input  B3,
  input  A4,
  input  B4,
  input  A5,
  input  B5,
  input  A6,
  input  B6,
  input  A7,
  input  B7,
  output S0,
  output S1,
  output S2,
  output S3,
  output S4,
  output S5,
  output S6,
  output S7,
  output C_OUT
);

  wire four_bit_full_adder_74ls283_1_c_out;

  Four_Bit_Full_Adder_74LS283 four_bit_full_adder_74ls283_1 (
    .S1(S1), .S0(S0), .B3(B3), .A3(A3), .B2(B2), .A2(A2), .B1(B1), .A1(A1), .B0(B0), .A0(A0), .C_IN(C_IN),
    .S2(S2), .S3(S3), .C_OUT(four_bit_full_adder_74ls283_1_c_out));
  Four_Bit_Full_Adder_74LS283 four_bit_full_adder_74ls283_2 (
    .S1(S5), .S0(S4), .B3(B7), .A3(A7), .B2(B6), .A2(A6), .B1(B5), .A1(A5), .B0(B4), .A0(A4),
    .C_IN(four_bit_full_adder_74ls283_1_c_out), .S2(S6), .S3(S7), .C_OUT(C_OUT));
endmodule

// 8-BIT FULL ADDER W/ SUB
module Eight_Bit_Full_Adder_w_Sub (
  input  ADD_SUB,
  input  A0,
  input  B0,
  input  A1,
  input  B1,
  input  A2,
  input  B2,
  input  A3,
  input  B3,
  input  A4,
  input  B4,
  input  A5,
  input  B5,
  input  A6,
  input  B6,
  input  A7,
  input  B7,
  output S0,
  output S1,
  output S2,
  output S3,
  output S4,
  output S5,
  output S6,
  output S7,
  output C_OUT
);

  wire xor_1_out, xor_2_out, xor_3_out, xor_4_out, xor_5_out, xor_6_out, xor_7_out, xor_8_out;

  xor xor_1 (xor_1_out, B0, ADD_SUB);
  xor xor_2 (xor_2_out, B1, ADD_SUB);
  xor xor_3 (xor_3_out, B2, ADD_SUB);
  xor xor_4 (xor_4_out, B3, ADD_SUB);
  xor xor_5 (xor_5_out, B4, ADD_SUB);
  xor xor_6 (xor_6_out, B5, ADD_SUB);
  xor xor_7 (xor_7_out, B6, ADD_SUB);
  xor xor_8 (xor_8_out, B7, ADD_SUB);
  Eight_Bit_Full_Adder_2x74LS283 eight_bit_full_adder_2x74ls283_1 (
    .C_IN(ADD_SUB), .A0(A0), .B0(xor_1_out), .A1(A1), .B1(xor_2_out), .A2(A2), .B2(xor_3_out), .A3(A3),
    .B3(xor_4_out), .A4(A4), .B4(xor_5_out), .A5(A5), .B5(xor_6_out), .A6(A6), .B6(xor_7_out), .A7(A7),
    .B7(xor_8_out), .S0(S0), .S1(S1), .S2(S2), .S3(S3), .S4(S4), .S5(S5), .S6(S6), .S7(S7), .C_OUT(C_OUT));
endmodule

// BUFFER
module Four_Bit_Buffer (
  input  E,
  input  A0,
  input  A1,
  input  A2,
  input  A3,
  output S0,
  output S1,
  output S2,
  output S3
);

  assign S0 = E ? A0 : 1'bz;  // Controlled_Buffer controlled_buffer_1
  assign S1 = E ? A1 : 1'bz;  // Controlled_Buffer controlled_buffer_2
  assign S2 = E ? A2 : 1'bz;  // Controlled_Buffer controlled_buffer_3
  assign S3 = E ? A3 : 1'bz;  // Controlled_Buffer controlled_buffer_4
endmodule

// BUFFER
module Eight_Bit_Buffer (
  input  E,
  input  A0,
  input  A1,
  input  A2,
  input  A3,
  input  A4,
  input  A5,
  input  A6,
  input  A7,
  output S0,
  output S1,
  output S2,
  output S3,
  output S4,
  output S5,
  output S6,
  output S7
);

  assign S0 = E ? A0 : 1'bz;  // Controlled_Buffer controlled_buffer_1
  assign S1 = E ? A1 : 1'bz;  // Controlled_Buffer controlled_buffer_2
  assign S2 = E ? A2 : 1'bz;  // Controlled_Buffer controlled_buffer_3
  assign S3 = E ? A3 : 1'bz;  // Controlled_Buffer controlled_buffer_4
  assign S4 = E ? A4 : 1'bz;  // Controlled_Buffer controlled_buffer_5
  assign S5 = E ? A5 : 1'bz;  // Controlled_Buffer controlled_buffer_6
  assign S6 = E ? A6 : 1'bz;  // Controlled_Buffer controlled_buffer_7
  assign S7 = E ? A7 : 1'bz;  // Controlled_Buffer controlled_buffer_8
endmodule

// D_TYPE
module D_Type_Flip_Flop_Rising_Edge (
  input  CLR,
  input  D,
  input  CLK,
  input  PRE,
  output Q,
  output NOT_Q
);

  wire nand_1_out, nand_2_out, nand_3_out, nand_4_out, not_1_out, not_2_out;

  not not_1 (not_1_out, CLR);
  not not_2 (not_2_out, PRE);
  nand nand_1 (nand_1_out, nand_4_out, not_2_out, nand_2_out);
  nand nand_2 (nand_2_out, nand_1_out, not_1_out, CLK);
  nand nand_3 (nand_3_out, nand_2_out, CLK, nand_4_out);
  nand nand_4 (nand_4_out, nand_3_out, not_1_out, D);
  nand nand_5 (Q, nand_2_out, not_2_out, NOT_Q);
  nand nand_6 (NOT_Q, Q, not_1_out, nand_3_out);
endmodule

// 4 BIT COUNT
module Four_Bit_Synchronous_Up_Counter (
  input  INC,
  input  CLEAR,
  input  CLK,
  output Q0,
  output Q1,
  output Q2,
  output Q3,
  output CARRY
);

  wire and_1_out, and_2_out, and_3_out, xor_1_out, xor_2_out, xor_3_out, xor_4_out;

  xor xor_1 (xor_1_out, INC, Q0);
  and and_1 (and_1_out, INC, Q0);
  xor xor_2 (xor_2_out, and_1_out, Q1);
  D_Type_Flip_Flop_Rising_Edge d_type_flip_flop_rising_edge_1 (
    .D(xor_1_out), .CLK(CLK), .CLR(CLEAR), .Q(Q0));  // open: PRE, NOT_Q
  and and_2 (and_2_out, and_1_out, Q1);
  xor xor_3 (xor_3_out, and_2_out, Q2);
  D_Type_Flip_Flop_Rising_Edge d_type_flip_flop_rising_edge_2 (
    .D(xor_2_out), .CLK(CLK), .CLR(CLEAR), .Q(Q1));  // open: PRE, NOT_Q
  and and_3 (and_3_out, and_2_out, Q2);
  xor xor_4 (xor_4_out, and_3_out, Q3);
  D_Type_Flip_Flop_Rising_Edge d_type_flip_flop_rising_edge_3 (
    .D(xor_3_out), .CLK(CLK), .CLR(CLEAR), .Q(Q2));  // open: PRE, NOT_Q
  and and_4 (CARRY, and_3_out, Q3);
  D_Type_Flip_Flop_Rising_Edge d_type_flip_flop_rising_edge_4 (
    .D(xor_4_out), .CLK(CLK), .CLR(CLEAR), .Q(Q3));  // open: PRE, NOT_Q
endmodule

// COUNTER
module Four_Bit_Synchronous_Up_Counter_with_Load_74LS161 (
  input  INC,
  input  LOAD,
  input  CLEAR,
  input  CLK,
  input  D0,
  input  D1,
  input  D2,
  input  D3,
  output Q0,
  output Q1,
  output Q2,
  output Q3,
  output CARRY
);

  wire and_1_out, and_2_out, and_3_out, pull_resistor_1_node, quad_2_to_1_mux_1_bit_74ls157_1_s0,
       quad_2_to_1_mux_1_bit_74ls157_1_s1, quad_2_to_1_mux_1_bit_74ls157_1_s2,
       quad_2_to_1_mux_1_bit_74ls157_1_s3, xor_1_out, xor_2_out, xor_3_out, xor_4_out;

  xor xor_1 (xor_1_out, INC, Q0);
  Pull_Resistor #(.pull(1)) pull_resistor_1 (.node(pull_resistor_1_node));
  and and_1 (and_1_out, INC, Q0);
  xor xor_2 (xor_2_out, and_1_out, Q1);
  Quad_2_to_1_Mux_1_Bit_74LS157 quad_2_to_1_mux_1_bit_74ls157_1 (
    .SEL(LOAD), .ENABLE(pull_resistor_1_node), .B3(D0), .A3(xor_1_out), .B2(D1), .A2(xor_2_out), .B1(D2),
    .A1(xor_3_out), .B0(D3), .A0(xor_4_out), .S3(quad_2_to_1_mux_1_bit_74ls157_1_s3),
    .S2(quad_2_to_1_mux_1_bit_74ls157_1_s2), .S1(quad_2_to_1_mux_1_bit_74ls157_1_s1),
    .S0(quad_2_to_1_mux_1_bit_74ls157_1_s0));
  D_Type_Flip_Flop_Rising_Edge d_type_flip_flop_rising_edge_1 (
    .D(quad_2_to_1_mux_1_bit_74ls157_1_s3), .CLK(CLK), .CLR(CLEAR), .Q(Q0));  // open: PRE, NOT_Q
  and and_2 (and_2_out, and_1_out, Q1);
  xor xor_3 (xor_3_out, and_2_out, Q2);
  D_Type_Flip_Flop_Rising_Edge d_type_flip_flop_rising_edge_2 (
    .D(quad_2_to_1_mux_1_bit_74ls157_1_s2), .CLK(CLK), .CLR(CLEAR), .Q(Q1));  // open: PRE, NOT_Q
  and and_3 (and_3_out, and_2_out, Q2);
  xor xor_4 (xor_4_out, and_3_out, Q3);
  D_Type_Flip_Flop_Rising_Edge d_type_flip_flop_rising_edge_3 (
    .D(quad_2_to_1_mux_1_bit_74ls157_1_s1), .CLK(CLK), .CLR(CLEAR), .Q(Q2));  // open: PRE, NOT_Q
  and and_4 (CARRY, and_3_out, Q3);
  D_Type_Flip_Flop_Rising_Edge d_type_flip_flop_rising_edge_4 (
    .D(quad_2_to_1_mux_1_bit_74ls157_1_s0), .CLK(CLK), .CLR(CLEAR), .Q(Q3));  // open: PRE, NOT_Q
endmodule

module Two_to_1_Mux_1_Bit (
  input  A0,
  input  B0,
  input  SEL,
  input  ENABLE,
  output OUT
);

  wire and_1_out, and_2_out, not_1_out;

  not not_1 (not_1_out, SEL);
  and and_1 (and_1_out, A0, not_1_out, ENABLE);
  and and_2 (and_2_out, B0, SEL, ENABLE);
  or or_1 (OUT, and_1_out, and_2_out);
endmodule

// SELECTOR
module Quad_2_to_1_Mux_1_Bit_74LS157 (
  input  SEL,
  input  ENABLE,
  input  B3,
  input  A3,
  input  B2,
  input  A2,
  input  B1,
  input  A1,
  input  B0,
  input  A0,
  output S3,
  output S2,
  output S1,
  output S0
);

  wire and_1_out, and_2_out, and_3_out, and_4_out, and_5_out, and_6_out, and_7_out, and_8_out, and_9_out,
       and_10_out, not_1_out;

  and and_1 (and_1_out, SEL, ENABLE);
  not not_1 (not_1_out, SEL);
  and and_2 (and_2_out, not_1_out, ENABLE);
  and and_3 (and_3_out, and_1_out, B3);
  and and_4 (and_4_out, and_2_out, A3);
  and and_5 (and_5_out, and_1_out, B2);
  and and_6 (and_6_out, and_2_out, A2);
  and and_7 (and_7_out, and_1_out, B1);
  and and_8 (and_8_out, and_2_out, A1);
  and and_9 (and_9_out, and_1_out, B0);
  and and_10 (and_10_out, and_2_out, A0);
  or or_1 (S3, and_3_out, and_4_out);
  or or_2 (S2, and_5_out, and_6_out);
  or or_3 (S1, and_7_out, and_8_out);
  or or_4 (S0, and_9_out, and_10_out);
endmodule

// 4 TO 1 MUX 4-BIT
module Four_to_1_Mux_4_Bit (
  input  A3,
  input  A2,
  input  A1,
  input  A0,
  input  B3,
  input  B2,
  input  B1,
  input  B0,
  input  ENABLE,
  input  C3,
  input  C2,
  input  C1,
  input  C0,
  input  D3,
  input  D2,
  input  D1,
  input  D0,
  input  S1,
  input  S0,
  output Q0,
  output Q1,
  output Q2,
  output Q3
);

  wire SEL1_s0, SEL1_s1, SEL1_s2, SEL1_s3, SEL2_s0, SEL2_s1, SEL2_s2, SEL2_s3;

  Quad_2_to_1_Mux_1_Bit_74LS157 SEL1 (
    .SEL(S0), .ENABLE(ENABLE), .B3(B3), .A3(A3), .B2(B2), .A2(A2), .B1(B1), .A1(A1), .B0(B0), .A0(A0),
    .S3(SEL1_s3), .S2(SEL1_s2), .S1(SEL1_s1), .S0(SEL1_s0));
  Quad_2_to_1_Mux_1_Bit_74LS157 SEL2 (
    .SEL(S0), .ENABLE(ENABLE), .B3(D3), .A3(C3), .B2(D2), .A2(C2), .B1(D1), .A1(C1), .B0(D0), .A0(C0),
    .S3(SEL2_s3), .S2(SEL2_s2), .S1(SEL2_s1), .S0(SEL2_s0));
  Quad_2_to_1_Mux_1_Bit_74LS157 SEL3 (
    .SEL(S1), .ENABLE(ENABLE), .B3(SEL2_s3), .A3(SEL1_s3), .B2(SEL2_s2), .A2(SEL1_s2), .B1(SEL2_s1),
    .A1(SEL1_s1), .B0(SEL2_s0), .A0(SEL1_s0), .S3(Q3), .S2(Q2), .S1(Q1), .S0(Q0));
endmodule

// 16-to-1 Mux (4-Bit Width)
module Sixteen_to_1_Mux_4_Bit (
  input  D0,
  input  D16,
  input  D1,
  input  D17,
  input  D2,
  input  D18,
  input  D3,
  input  D19,
  input  D4,
  input  D20,
  input  D5,
  input  D21,
  input  D6,
  input  D22,
  input  D7,
  input  D23,
  input  D8,
  input  D24,
  input  D9,
  input  D25,
  input  D10,
  input  D26,
  input  D11,
  input  D27,
  input  D12,
  input  D28,
  input  D13,
  input  D29,
  input  D14,
  input  D30,
  input  D15,
  input  D31,
  input  D32,
  input  D48,
  input  D33,
  input  D49,
  input  D34,
  input  D50,
  input  D35,
  input  D51,
  input  D36,
  input  D52,
  input  D37,
  input  D53,
  input  D38,
  input  D54,
  input  D39,
  input  D55,
  input  D40,
  input  D56,
  input  D41,
  input  D57,
  input  D42,
  input  D58,
  input  D43,
  input  D59,
  input  D44,
  input  D60,
  input  D45,
  input  D61,
  input  D46,
  input  D62,
  input  D47,
  input  D63,
  input  ENABLE,
  input  A3,
  input  A2,
  input  A1,
  input  A0,
  output S0,
  output S1,
  output S2,
  output S3
);

  wire [3:0] MUX1_q0, MUX2_q0, MUX3_q0, MUX4_q0;

  Four_to_1_Mux_4_Bit MUX1 (
    .Q3(MUX1_q0[3]), .Q2(MUX1_q0[2]), .Q1(MUX1_q0[1]), .Q0(MUX1_q0[0]), .A3(D3), .C3(D11), .A2(D2), .C2(D10),
    .A1(D1), .C1(D9), .A0(D0), .C0(D8), .B3(D7), .D3(D15), .B2(D6), .D2(D14), .B1(D5), .D1(D13), .B0(D4),
    .D0(D12), .ENABLE(ENABLE), .S1(A1), .S0(A0));
  Four_to_1_Mux_4_Bit MUX3 (
    .Q3(MUX3_q0[3]), .Q2(MUX3_q0[2]), .Q1(MUX3_q0[1]), .Q0(MUX3_q0[0]), .A3(D35), .C3(D43), .A2(D34),
    .C2(D42), .A1(D33), .C1(D41), .A0(D32), .C0(D40), .B3(D39), .D3(D47), .B2(D38), .D2(D46), .B1(D37),
    .D1(D45), .B0(D36), .D0(D44), .ENABLE(ENABLE), .S1(A1), .S0(A0));
  Four_to_1_Mux_4_Bit MUX2 (
    .Q3(MUX2_q0[3]), .Q2(MUX2_q0[2]), .Q1(MUX2_q0[1]), .Q0(MUX2_q0[0]), .A3(D19), .C3(D27), .A2(D18),
    .C2(D26), .A1(D17), .C1(D25), .A0(D16), .C0(D24), .B3(D23), .D3(D31), .B2(D22), .D2(D30), .B1(D21),
    .D1(D29), .B0(D20), .D0(D28), .ENABLE(ENABLE), .S1(A1), .S0(A0));
  Four_to_1_Mux_4_Bit MUX4 (
    .Q3(MUX4_q0[3]), .Q2(MUX4_q0[2]), .Q1(MUX4_q0[1]), .Q0(MUX4_q0[0]), .A3(D51), .C3(D59), .A2(D50),
    .C2(D58), .A1(D49), .C1(D57), .A0(D48), .C0(D56), .B3(D55), .D3(D63), .B2(D54), .D2(D62), .B1(D53),
    .D1(D61), .B0(D52), .D0(D60), .ENABLE(ENABLE), .S1(A1), .S0(A0));
  Four_to_1_Mux_4_Bit MUX5 (
    .Q3(S3), .Q2(S2), .Q1(S1), .Q0(S0), .A3(MUX1_q0[3]), .C3(MUX3_q0[3]), .A2(MUX1_q0[2]), .C2(MUX3_q0[2]),
    .A1(MUX1_q0[1]), .C1(MUX3_q0[1]), .A0(MUX1_q0[0]), .C0(MUX3_q0[0]), .B3(MUX2_q0[3]), .D3(MUX4_q0[3]),
    .B2(MUX2_q0[2]), .D2(MUX4_q0[2]), .B1(MUX2_q0[1]), .D1(MUX4_q0[1]), .B0(MUX2_q0[0]), .D0(MUX4_q0[0]),
    .ENABLE(ENABLE), .S1(A3), .S0(A2));
endmodule

// REG
module One_Bit_Register (
  input  LOAD,
  input  CLR,
  input  CLK,
  input  A0,
  output Q,
  output NOT_Q
);

  wire and_1_out, and_2_out, not_1_out, or_1_out;

  not not_1 (not_1_out, LOAD);
  and and_1 (and_1_out, Q, not_1_out);
  and and_2 (and_2_out, LOAD, A0);
  or or_1 (or_1_out, and_1_out, and_2_out);
  D_Type_Flip_Flop_Rising_Edge d_type_flip_flop_rising_edge_1 (
    .D(or_1_out), .CLK(CLK), .CLR(CLR), .Q(Q), .NOT_Q(NOT_Q));  // open: PRE
endmodule

// REG
module Four_Bit_Register (
  input  A0,
  input  A1,
  input  A2,
  input  A3,
  input  CLR,
  input  LOAD,
  input  CLK,
  output S0,
  output S1,
  output S2,
  output S3
);

  One_Bit_Register L_1_Bit_Register_1 (.CLR(CLR), .A0(A0), .LOAD(LOAD), .CLK(CLK), .Q(S0));  // open: NOT_Q
  One_Bit_Register L_1_Bit_Register_2 (.CLR(CLR), .A0(A1), .LOAD(LOAD), .CLK(CLK), .Q(S1));  // open: NOT_Q
  One_Bit_Register L_1_Bit_Register_3 (.CLR(CLR), .A0(A2), .LOAD(LOAD), .CLK(CLK), .Q(S2));  // open: NOT_Q
  One_Bit_Register L_1_Bit_Register_4 (.CLR(CLR), .A0(A3), .LOAD(LOAD), .CLK(CLK), .Q(S3));  // open: NOT_Q
endmodule

// REG
module Four_Bit_Buffered_Register_74LS173 (
  input  A0,
  input  A1,
  input  A2,
  input  A3,
  input  CLR,
  input  LOAD,
  input  CLK,
  input  ENABLE,
  output S0,
  output S1,
  output S2,
  output S3
);

  wire four_bit_register_1_s0, four_bit_register_1_s1, four_bit_register_1_s2, four_bit_register_1_s3;

  Four_Bit_Register four_bit_register_1 (
    .A0(A0), .A1(A1), .A2(A2), .A3(A3), .CLR(CLR), .LOAD(LOAD), .CLK(CLK), .S0(four_bit_register_1_s0),
    .S1(four_bit_register_1_s1), .S2(four_bit_register_1_s2), .S3(four_bit_register_1_s3));
  Four_Bit_Buffer four_bit_buffer_1 (
    .A0(four_bit_register_1_s0), .A1(four_bit_register_1_s1), .A2(four_bit_register_1_s2),
    .A3(four_bit_register_1_s3), .E(ENABLE), .S0(S0), .S1(S1), .S2(S2), .S3(S3));
endmodule

// REGISTER
module Eight_Bit_Register (
  input  A0,
  input  A1,
  input  A2,
  input  A3,
  input  A4,
  input  A5,
  input  A6,
  input  A7,
  input  CLR,
  input  LOAD,
  input  CLK,
  output S0,
  output S1,
  output S2,
  output S3,
  output S4,
  output S5,
  output S6,
  output S7
);

  One_Bit_Register one_bit_register_1 (.CLR(CLR), .A0(A0), .LOAD(LOAD), .CLK(CLK), .Q(S0));  // open: NOT_Q
  One_Bit_Register one_bit_register_2 (.CLR(CLR), .A0(A1), .LOAD(LOAD), .CLK(CLK), .Q(S1));  // open: NOT_Q
  One_Bit_Register one_bit_register_3 (.CLR(CLR), .A0(A2), .LOAD(LOAD), .CLK(CLK), .Q(S2));  // open: NOT_Q
  One_Bit_Register one_bit_register_4 (.CLR(CLR), .A0(A3), .LOAD(LOAD), .CLK(CLK), .Q(S3));  // open: NOT_Q
  One_Bit_Register one_bit_register_5 (.CLR(CLR), .A0(A4), .LOAD(LOAD), .CLK(CLK), .Q(S4));  // open: NOT_Q
  One_Bit_Register one_bit_register_6 (.CLR(CLR), .A0(A5), .LOAD(LOAD), .CLK(CLK), .Q(S5));  // open: NOT_Q
  One_Bit_Register one_bit_register_7 (.CLR(CLR), .A0(A6), .LOAD(LOAD), .CLK(CLK), .Q(S6));  // open: NOT_Q
  One_Bit_Register one_bit_register_8 (.CLR(CLR), .A0(A7), .LOAD(LOAD), .CLK(CLK), .Q(S7));  // open: NOT_Q
endmodule

// REG
module Eight_Bit_Buffered_Register_2x74LS173 (
  input  A0,
  input  A1,
  input  A2,
  input  A3,
  input  A4,
  input  A5,
  input  A6,
  input  A7,
  input  CLR,
  input  LOAD,
  input  CLK,
  input  ENABLE,
  output S0,
  output S1,
  output S2,
  output S3,
  output S4,
  output S5,
  output S6,
  output S7
);

  wire eight_bit_register_1_s0, eight_bit_register_1_s1, eight_bit_register_1_s2, eight_bit_register_1_s3,
       eight_bit_register_1_s4, eight_bit_register_1_s5, eight_bit_register_1_s6, eight_bit_register_1_s7;

  Eight_Bit_Register eight_bit_register_1 (
    .A0(A0), .A1(A1), .A2(A2), .A3(A3), .A4(A4), .A5(A5), .A6(A6), .A7(A7), .CLR(CLR), .LOAD(LOAD),
    .CLK(CLK), .S0(eight_bit_register_1_s0), .S1(eight_bit_register_1_s1), .S2(eight_bit_register_1_s2),
    .S3(eight_bit_register_1_s3), .S4(eight_bit_register_1_s4), .S5(eight_bit_register_1_s5),
    .S6(eight_bit_register_1_s6), .S7(eight_bit_register_1_s7));
  Eight_Bit_Buffer eight_bit_buffer_1 (
    .A0(eight_bit_register_1_s0), .A1(eight_bit_register_1_s1), .A2(eight_bit_register_1_s2),
    .A3(eight_bit_register_1_s3), .A4(eight_bit_register_1_s4), .A5(eight_bit_register_1_s5),
    .A6(eight_bit_register_1_s6), .A7(eight_bit_register_1_s7), .E(ENABLE), .S0(S0), .S1(S1), .S2(S2),
    .S3(S3), .S4(S4), .S5(S5), .S6(S6), .S7(S7));
endmodule

// 2 TO 4
module Two_to_4_Line_Decoder_1_Bit (
  input  A0,
  input  ENABLE,
  input  A1,
  output D0,
  output D1,
  output D2,
  output D3
);

  wire not_1_out, not_2_out;

  not not_1 (not_1_out, A0);
  not not_2 (not_2_out, A1);
  and and_1 (D0, not_1_out, ENABLE, not_2_out);
  and and_2 (D1, A0, ENABLE, not_2_out);
  and and_3 (D2, A1, ENABLE, not_1_out);
  and and_4 (D3, A1, ENABLE, A0);
endmodule

// 4-to-16 Line Decoder
module Four_to_16_Line_Decoder_1_Bit (
  input  ENABLE,
  input  A0,
  input  A1,
  input  A2,
  input  A3,
  output Q0,
  output Q1,
  output Q2,
  output Q3,
  output Q4,
  output Q5,
  output Q6,
  output Q7,
  output Q8,
  output Q9,
  output Q10,
  output Q11,
  output Q12,
  output Q13,
  output Q14,
  output Q15
);

  wire two_to_4_line_decoder_1_bit_1_d0, two_to_4_line_decoder_1_bit_1_d1, two_to_4_line_decoder_1_bit_1_d2,
       two_to_4_line_decoder_1_bit_1_d3;

  Two_to_4_Line_Decoder_1_Bit two_to_4_line_decoder_1_bit_1 (
    .A0(A2), .ENABLE(ENABLE), .A1(A3), .D0(two_to_4_line_decoder_1_bit_1_d0),
    .D1(two_to_4_line_decoder_1_bit_1_d1), .D2(two_to_4_line_decoder_1_bit_1_d2),
    .D3(two_to_4_line_decoder_1_bit_1_d3));
  Two_to_4_Line_Decoder_1_Bit two_to_4_line_decoder_1_bit_2 (
    .A0(A0), .ENABLE(two_to_4_line_decoder_1_bit_1_d0), .A1(A1), .D0(Q0), .D1(Q1), .D2(Q2), .D3(Q3));
  Two_to_4_Line_Decoder_1_Bit two_to_4_line_decoder_1_bit_3 (
    .A0(A0), .ENABLE(two_to_4_line_decoder_1_bit_1_d1), .A1(A1), .D0(Q4), .D1(Q5), .D2(Q6), .D3(Q7));
  Two_to_4_Line_Decoder_1_Bit two_to_4_line_decoder_1_bit_4 (
    .A0(A0), .ENABLE(two_to_4_line_decoder_1_bit_1_d2), .A1(A1), .D0(Q8), .D1(Q9), .D2(Q10), .D3(Q11));
  Two_to_4_Line_Decoder_1_Bit two_to_4_line_decoder_1_bit_5 (
    .A0(A0), .ENABLE(two_to_4_line_decoder_1_bit_1_d3), .A1(A1), .D0(Q12), .D1(Q13), .D2(Q14), .D3(Q15));
endmodule

// RAM
module RAM64_16_word_4_Bit_74189 (
  input  WRITE_ENABLE,
  input  CLR,
  input  D0,
  input  D1,
  input  D2,
  input  D3,
  input  A0,
  input  A1,
  input  A2,
  input  A3,
  output S0,
  output S1,
  output S2,
  output S3
);

  wire DEC1_q0, DEC1_q1, DEC1_q2, DEC1_q3, DEC1_q4, DEC1_q5, DEC1_q6, DEC1_q7, DEC1_q8, DEC1_q9, DEC1_q10,
       DEC1_q11, DEC1_q12, DEC1_q13, DEC1_q14, DEC1_q15, not_1_out;
  wire [3:0] REG1_s0, REG2_s0, REG3_s0, REG4_s0, REG5_s0, REG6_s0, REG7_s0, REG8_s0, REG9_s0, REG10_s0,
       REG11_s0, REG12_s0, REG13_s0, REG14_s0, REG15_s0, REG16_s0;

  Four_to_16_Line_Decoder_1_Bit DEC1 (
    .A0(A0), .A1(A1), .A2(A2), .A3(A3), .ENABLE(WRITE_ENABLE), .Q0(DEC1_q0), .Q1(DEC1_q1), .Q2(DEC1_q2),
    .Q3(DEC1_q3), .Q4(DEC1_q4), .Q5(DEC1_q5), .Q6(DEC1_q6), .Q7(DEC1_q7), .Q8(DEC1_q8), .Q9(DEC1_q9),
    .Q10(DEC1_q10), .Q11(DEC1_q11), .Q12(DEC1_q12), .Q13(DEC1_q13), .Q14(DEC1_q14), .Q15(DEC1_q15));
  not not_1 (not_1_out, WRITE_ENABLE);
  Four_Bit_Register REG1 (
    .A0(D0), .A1(D1), .A2(D2), .A3(D3), .CLR(CLR), .LOAD(WRITE_ENABLE), .CLK(DEC1_q0), .S0(REG1_s0[0]),
    .S1(REG1_s0[1]), .S2(REG1_s0[2]), .S3(REG1_s0[3]));
  Four_Bit_Register REG3 (
    .A0(D0), .A1(D1), .A2(D2), .A3(D3), .CLR(CLR), .LOAD(WRITE_ENABLE), .CLK(DEC1_q2), .S0(REG3_s0[0]),
    .S1(REG3_s0[1]), .S2(REG3_s0[2]), .S3(REG3_s0[3]));
  Four_Bit_Register REG5 (
    .A0(D0), .A1(D1), .A2(D2), .A3(D3), .CLR(CLR), .LOAD(WRITE_ENABLE), .CLK(DEC1_q4), .S0(REG5_s0[0]),
    .S1(REG5_s0[1]), .S2(REG5_s0[2]), .S3(REG5_s0[3]));
  Four_Bit_Register REG7 (
    .A0(D0), .A1(D1), .A2(D2), .A3(D3), .CLR(CLR), .LOAD(WRITE_ENABLE), .CLK(DEC1_q6), .S0(REG7_s0[0]),
    .S1(REG7_s0[1]), .S2(REG7_s0[2]), .S3(REG7_s0[3]));
  Four_Bit_Register REG2 (
    .A0(D0), .A1(D1), .A2(D2), .A3(D3), .CLR(CLR), .LOAD(WRITE_ENABLE), .CLK(DEC1_q1), .S0(REG2_s0[0]),
    .S1(REG2_s0[1]), .S2(REG2_s0[2]), .S3(REG2_s0[3]));
  Four_Bit_Register REG4 (
    .A0(D0), .A1(D1), .A2(D2), .A3(D3), .CLR(CLR), .LOAD(WRITE_ENABLE), .CLK(DEC1_q3), .S0(REG4_s0[0]),
    .S1(REG4_s0[1]), .S2(REG4_s0[2]), .S3(REG4_s0[3]));
  Four_Bit_Register REG6 (
    .A0(D0), .A1(D1), .A2(D2), .A3(D3), .CLR(CLR), .LOAD(WRITE_ENABLE), .CLK(DEC1_q5), .S0(REG6_s0[0]),
    .S1(REG6_s0[1]), .S2(REG6_s0[2]), .S3(REG6_s0[3]));
  Four_Bit_Register REG8 (
    .A0(D0), .A1(D1), .A2(D2), .A3(D3), .CLR(CLR), .LOAD(WRITE_ENABLE), .CLK(DEC1_q7), .S0(REG8_s0[0]),
    .S1(REG8_s0[1]), .S2(REG8_s0[2]), .S3(REG8_s0[3]));
  Four_Bit_Register REG9 (
    .A0(D0), .A1(D1), .A2(D2), .A3(D3), .CLR(CLR), .LOAD(WRITE_ENABLE), .CLK(DEC1_q8), .S0(REG9_s0[0]),
    .S1(REG9_s0[1]), .S2(REG9_s0[2]), .S3(REG9_s0[3]));
  Four_Bit_Register REG11 (
    .A0(D0), .A1(D1), .A2(D2), .A3(D3), .CLR(CLR), .LOAD(WRITE_ENABLE), .CLK(DEC1_q10), .S0(REG11_s0[0]),
    .S1(REG11_s0[1]), .S2(REG11_s0[2]), .S3(REG11_s0[3]));
  Four_Bit_Register REG13 (
    .A0(D0), .A1(D1), .A2(D2), .A3(D3), .CLR(CLR), .LOAD(WRITE_ENABLE), .CLK(DEC1_q12), .S0(REG13_s0[0]),
    .S1(REG13_s0[1]), .S2(REG13_s0[2]), .S3(REG13_s0[3]));
  Four_Bit_Register REG15 (
    .A0(D0), .A1(D1), .A2(D2), .A3(D3), .CLR(CLR), .LOAD(WRITE_ENABLE), .CLK(DEC1_q14), .S0(REG15_s0[0]),
    .S1(REG15_s0[1]), .S2(REG15_s0[2]), .S3(REG15_s0[3]));
  Four_Bit_Register REG10 (
    .A0(D0), .A1(D1), .A2(D2), .A3(D3), .CLR(CLR), .LOAD(WRITE_ENABLE), .CLK(DEC1_q9), .S0(REG10_s0[0]),
    .S1(REG10_s0[1]), .S2(REG10_s0[2]), .S3(REG10_s0[3]));
  Four_Bit_Register REG12 (
    .A0(D0), .A1(D1), .A2(D2), .A3(D3), .CLR(CLR), .LOAD(WRITE_ENABLE), .CLK(DEC1_q11), .S0(REG12_s0[0]),
    .S1(REG12_s0[1]), .S2(REG12_s0[2]), .S3(REG12_s0[3]));
  Four_Bit_Register REG14 (
    .A0(D0), .A1(D1), .A2(D2), .A3(D3), .CLR(CLR), .LOAD(WRITE_ENABLE), .CLK(DEC1_q13), .S0(REG14_s0[0]),
    .S1(REG14_s0[1]), .S2(REG14_s0[2]), .S3(REG14_s0[3]));
  Four_Bit_Register REG16 (
    .A0(D0), .A1(D1), .A2(D2), .A3(D3), .CLR(CLR), .LOAD(WRITE_ENABLE), .CLK(DEC1_q15), .S0(REG16_s0[0]),
    .S1(REG16_s0[1]), .S2(REG16_s0[2]), .S3(REG16_s0[3]));
  Sixteen_to_1_Mux_4_Bit MUX1 (
    .D0(REG1_s0[0]), .D16(REG5_s0[0]), .D1(REG1_s0[1]), .D17(REG5_s0[1]), .D2(REG1_s0[2]), .D18(REG5_s0[2]),
    .D3(REG1_s0[3]), .D19(REG5_s0[3]), .D4(REG2_s0[0]), .D20(REG6_s0[0]), .D5(REG2_s0[1]), .D21(REG6_s0[1]),
    .D6(REG2_s0[2]), .D22(REG6_s0[2]), .D7(REG2_s0[3]), .D23(REG6_s0[3]), .D8(REG3_s0[0]), .D24(REG7_s0[0]),
    .D9(REG3_s0[1]), .D25(REG7_s0[1]), .D10(REG3_s0[2]), .D26(REG7_s0[2]), .D11(REG3_s0[3]),
    .D27(REG7_s0[3]), .D12(REG4_s0[0]), .D28(REG8_s0[0]), .D13(REG4_s0[1]), .D29(REG8_s0[1]),
    .D14(REG4_s0[2]), .D30(REG8_s0[2]), .D15(REG4_s0[3]), .D31(REG8_s0[3]), .D32(REG9_s0[0]),
    .D48(REG13_s0[0]), .D33(REG9_s0[1]), .D49(REG13_s0[1]), .D34(REG9_s0[2]), .D50(REG13_s0[2]),
    .D35(REG9_s0[3]), .D51(REG13_s0[3]), .D36(REG10_s0[0]), .D52(REG14_s0[0]), .D37(REG10_s0[1]),
    .D53(REG14_s0[1]), .D38(REG10_s0[2]), .D54(REG14_s0[2]), .D39(REG10_s0[3]), .D55(REG14_s0[3]),
    .D40(REG11_s0[0]), .D56(REG15_s0[0]), .D41(REG11_s0[1]), .D57(REG15_s0[1]), .D42(REG11_s0[2]),
    .D58(REG15_s0[2]), .D43(REG11_s0[3]), .D59(REG15_s0[3]), .D44(REG12_s0[0]), .D60(REG16_s0[0]),
    .D45(REG12_s0[1]), .D61(REG16_s0[1]), .D46(REG12_s0[2]), .D62(REG16_s0[2]), .D47(REG12_s0[3]),
    .D63(REG16_s0[3]), .ENABLE(not_1_out), .S0(S0), .S1(S1), .S2(S2), .S3(S3), .A3(A3), .A2(A2), .A1(A1),
    .A0(A0));
endmodule

// REG
module A_B_Reg (
  input  [7:0] DATA_IN,
  input  AI,
  input  CLK,
  input  CLR,
  input  AO,
  output [7:0] BUS,
  output [7:0] A0_A7
);

  wire pull_resistor_1_node;

  Eight_Bit_Buffer eight_bit_buffer_1 (
    .A0(A0_A7[0]), .A1(A0_A7[1]), .A2(A0_A7[2]), .A3(A0_A7[3]), .A4(A0_A7[4]), .A5(A0_A7[5]), .A6(A0_A7[6]),
    .A7(A0_A7[7]), .E(AO), .S0(BUS[0]), .S1(BUS[1]), .S2(BUS[2]), .S3(BUS[3]), .S4(BUS[4]), .S5(BUS[5]),
    .S6(BUS[6]), .S7(BUS[7]));
  Pull_Resistor #(.pull(1)) pull_resistor_1 (.node(pull_resistor_1_node));
  Eight_Bit_Buffered_Register_2x74LS173 eight_bit_buffered_register_2x74ls173_1 (
    .A0(DATA_IN[0]), .A1(DATA_IN[1]), .A2(DATA_IN[2]), .A3(DATA_IN[3]), .A4(DATA_IN[4]), .A5(DATA_IN[5]),
    .A6(DATA_IN[6]), .A7(DATA_IN[7]), .CLR(CLR), .LOAD(AI), .CLK(CLK), .ENABLE(pull_resistor_1_node),
    .S0(A0_A7[0]), .S1(A0_A7[1]), .S2(A0_A7[2]), .S3(A0_A7[3]), .S4(A0_A7[4]), .S5(A0_A7[5]), .S6(A0_A7[6]),
    .S7(A0_A7[7]));
endmodule

// IR
module Instruction_Reg (
  input  [7:0] DATA_IN,
  input  II,
  input  CLK,
  input  CLR,
  input  IO,
  output [7:0] BUS,
  output [3:0] IR4_IR7
);

  wire eight_bit_buffered_register_2x74ls173_1_s0, eight_bit_buffered_register_2x74ls173_1_s1,
       eight_bit_buffered_register_2x74ls173_1_s2, eight_bit_buffered_register_2x74ls173_1_s3,
       pull_resistor_1_node;

  Eight_Bit_Buffer eight_bit_buffer_1 (
    .A0(eight_bit_buffered_register_2x74ls173_1_s0), .A1(eight_bit_buffered_register_2x74ls173_1_s1),
    .A2(eight_bit_buffered_register_2x74ls173_1_s2), .A3(eight_bit_buffered_register_2x74ls173_1_s3), .E(IO),
    .S0(BUS[0]), .S1(BUS[1]), .S2(BUS[2]), .S3(BUS[3]), .S4(BUS[4]), .S5(BUS[5]), .S6(BUS[6]), .S7(BUS[7]));  // open: A4, A5, A6, A7
  Pull_Resistor #(.pull(1)) pull_resistor_1 (.node(pull_resistor_1_node));
  Eight_Bit_Buffered_Register_2x74LS173 eight_bit_buffered_register_2x74ls173_1 (
    .A0(DATA_IN[0]), .A1(DATA_IN[1]), .A2(DATA_IN[2]), .A3(DATA_IN[3]), .A4(DATA_IN[4]), .A5(DATA_IN[5]),
    .A6(DATA_IN[6]), .A7(DATA_IN[7]), .CLR(CLR), .LOAD(II), .CLK(CLK), .ENABLE(pull_resistor_1_node),
    .S0(eight_bit_buffered_register_2x74ls173_1_s0), .S1(eight_bit_buffered_register_2x74ls173_1_s1),
    .S2(eight_bit_buffered_register_2x74ls173_1_s2), .S3(eight_bit_buffered_register_2x74ls173_1_s3),
    .S4(IR4_IR7[0]), .S5(IR4_IR7[1]), .S6(IR4_IR7[2]), .S7(IR4_IR7[3]));
endmodule

module ALU (
  input  SUB,
  input  EO,
  input  A0,
  input  A1,
  input  A2,
  input  A3,
  input  A4,
  input  A5,
  input  A6,
  input  A7,
  input  B0,
  input  B1,
  input  B2,
  input  B3,
  input  B4,
  input  B5,
  input  B6,
  input  FLAG_CLR,
  input  CLK,
  input  FI,
  input  B7,
  output [7:0] BUS,
  output CF,
  output ZF
);

  wire eight_bit_full_adder_w_sub_1_c_out, eight_bit_full_adder_w_sub_1_s0, eight_bit_full_adder_w_sub_1_s1,
       eight_bit_full_adder_w_sub_1_s2, eight_bit_full_adder_w_sub_1_s3, eight_bit_full_adder_w_sub_1_s4,
       eight_bit_full_adder_w_sub_1_s5, eight_bit_full_adder_w_sub_1_s6, eight_bit_full_adder_w_sub_1_s7,
       not_1_out, or_1_out, or_2_out, or_3_out, or_4_out, or_5_out, or_6_out, or_7_out, pull_resistor_1_node;

  Eight_Bit_Full_Adder_w_Sub eight_bit_full_adder_w_sub_1 (
    .ADD_SUB(SUB), .A0(A0), .B0(B0), .A1(A1), .B1(B1), .A2(A2), .B2(B2), .A3(A3), .B3(B3), .A4(A4), .B4(B4),
    .A5(A5), .B5(B5), .A6(A6), .B6(B6), .A7(A7), .B7(B7), .S0(eight_bit_full_adder_w_sub_1_s0),
    .S1(eight_bit_full_adder_w_sub_1_s1), .S2(eight_bit_full_adder_w_sub_1_s2),
    .S3(eight_bit_full_adder_w_sub_1_s3), .S4(eight_bit_full_adder_w_sub_1_s4),
    .S5(eight_bit_full_adder_w_sub_1_s5), .S6(eight_bit_full_adder_w_sub_1_s6),
    .S7(eight_bit_full_adder_w_sub_1_s7), .C_OUT(eight_bit_full_adder_w_sub_1_c_out));
  Eight_Bit_Buffer eight_bit_buffer_1 (
    .A0(eight_bit_full_adder_w_sub_1_s0), .A1(eight_bit_full_adder_w_sub_1_s1),
    .A2(eight_bit_full_adder_w_sub_1_s2), .A3(eight_bit_full_adder_w_sub_1_s3),
    .A4(eight_bit_full_adder_w_sub_1_s4), .A5(eight_bit_full_adder_w_sub_1_s5),
    .A6(eight_bit_full_adder_w_sub_1_s6), .A7(eight_bit_full_adder_w_sub_1_s7), .E(EO), .S0(BUS[0]),
    .S1(BUS[1]), .S2(BUS[2]), .S3(BUS[3]), .S4(BUS[4]), .S5(BUS[5]), .S6(BUS[6]), .S7(BUS[7]));
  or or_1 (or_1_out, eight_bit_full_adder_w_sub_1_s0, eight_bit_full_adder_w_sub_1_s1);
  or or_2 (or_2_out, eight_bit_full_adder_w_sub_1_s2, eight_bit_full_adder_w_sub_1_s3);
  or or_3 (or_3_out, eight_bit_full_adder_w_sub_1_s4, eight_bit_full_adder_w_sub_1_s5);
  or or_4 (or_4_out, eight_bit_full_adder_w_sub_1_s6, eight_bit_full_adder_w_sub_1_s7);
  or or_5 (or_5_out, or_1_out, or_2_out);
  or or_6 (or_6_out, or_5_out, or_7_out);
  or or_7 (or_7_out, or_3_out, or_4_out);
  not not_1 (not_1_out, or_6_out);
  Four_Bit_Buffered_Register_74LS173 four_bit_buffered_register_74ls173_1 (
    .A0(eight_bit_full_adder_w_sub_1_c_out), .A1(not_1_out), .S0(CF), .S1(ZF), .CLR(FLAG_CLR), .LOAD(FI),
    .CLK(CLK), .ENABLE(pull_resistor_1_node));  // open: A2, A3, S2, S3
  Pull_Resistor #(.pull(1)) pull_resistor_1 (.node(pull_resistor_1_node));
endmodule

// MAR
module Four_Bit_MAR (
  input  PROG,
  input  [3:0] DATA_IN,
  input  [3:0] BUS,
  input  CLR,
  input  MI,
  input  CLK,
  output [3:0] A0_A4
);

  wire four_bit_buffered_register_74ls173_1_s0, four_bit_buffered_register_74ls173_1_s1,
       four_bit_buffered_register_74ls173_1_s2, four_bit_buffered_register_74ls173_1_s3,
       pull_resistor_1_node, pull_resistor_2_node;

  Pull_Resistor #(.pull(1)) pull_resistor_1 (.node(pull_resistor_1_node));
  Four_Bit_Buffered_Register_74LS173 four_bit_buffered_register_74ls173_1 (
    .A0(BUS[0]), .A1(BUS[1]), .A2(BUS[2]), .A3(BUS[3]), .S0(four_bit_buffered_register_74ls173_1_s0),
    .S1(four_bit_buffered_register_74ls173_1_s1), .S2(four_bit_buffered_register_74ls173_1_s2),
    .S3(four_bit_buffered_register_74ls173_1_s3), .CLR(CLR), .LOAD(MI), .CLK(CLK),
    .ENABLE(pull_resistor_2_node));
  Pull_Resistor #(.pull(1)) pull_resistor_2 (.node(pull_resistor_2_node));
  Quad_2_to_1_Mux_1_Bit_74LS157 quad_2_to_1_mux_1_bit_74ls157_1 (
    .SEL(PROG), .ENABLE(pull_resistor_1_node), .B3(DATA_IN[3]), .A3(four_bit_buffered_register_74ls173_1_s3),
    .B2(DATA_IN[2]), .A2(four_bit_buffered_register_74ls173_1_s2), .B1(DATA_IN[1]),
    .A1(four_bit_buffered_register_74ls173_1_s1), .B0(DATA_IN[0]),
    .A0(four_bit_buffered_register_74ls173_1_s0), .S3(A0_A4[3]), .S2(A0_A4[2]), .S1(A0_A4[1]), .S0(A0_A4[0]));
endmodule

module RAM (
  input  A3,
  input  A2,
  input  A1,
  input  A0,
  input  CLR,
  input  TOGGLE,
  input  PROG,
  input  CLK,
  input  RI,
  input  RO,
  input  [7:0] DATA_IN,
  output [7:0] BUS_OUT
);

  wire and_1_out, pull_resistor_1_node, RAM1_s0, RAM1_s1, RAM1_s2, RAM1_s3, RAM2_s0, RAM2_s1, RAM2_s2,
       RAM2_s3, SEL1_s0;

  RAM64_16_word_4_Bit_74189 RAM1 (
    .D3(DATA_IN[3]), .D2(DATA_IN[2]), .D1(DATA_IN[1]), .D0(DATA_IN[0]), .A3(A3), .A2(A2), .A1(A1), .A0(A0),
    .S3(RAM1_s3), .S2(RAM1_s2), .S1(RAM1_s1), .S0(RAM1_s0), .WRITE_ENABLE(SEL1_s0), .CLR(CLR));
  Quad_2_to_1_Mux_1_Bit_74LS157 SEL1 (
    .SEL(PROG), .ENABLE(pull_resistor_1_node), .B0(TOGGLE), .A0(and_1_out), .S0(SEL1_s0));  // open: B3, A3, B2, A2, B1, A1, S3, S2, S1
  Pull_Resistor #(.pull(1)) pull_resistor_1 (.node(pull_resistor_1_node));
  and and_1 (and_1_out, RI, CLK);
  RAM64_16_word_4_Bit_74189 RAM2 (
    .D3(DATA_IN[7]), .D2(DATA_IN[6]), .D1(DATA_IN[5]), .D0(DATA_IN[4]), .A3(A3), .A2(A2), .A1(A1), .A0(A0),
    .S3(RAM2_s3), .S2(RAM2_s2), .S1(RAM2_s1), .S0(RAM2_s0), .WRITE_ENABLE(SEL1_s0), .CLR(CLR));
  Eight_Bit_Buffer BUF1 (
    .A0(RAM1_s0), .A1(RAM1_s1), .A2(RAM1_s2), .A3(RAM1_s3), .A4(RAM2_s0), .A5(RAM2_s1), .A6(RAM2_s2),
    .A7(RAM2_s3), .E(RO), .S0(BUS_OUT[0]), .S1(BUS_OUT[1]), .S2(BUS_OUT[2]), .S3(BUS_OUT[3]),
    .S4(BUS_OUT[4]), .S5(BUS_OUT[5]), .S6(BUS_OUT[6]), .S7(BUS_OUT[7]));
endmodule

// PC
module Program_Counter (
  input  [3:0] DATA_IN,
  input  CO,
  input  J,
  input  CLK,
  input  CE,
  input  CLR,
  output [3:0] BUS_OUT
);

  wire four_bit_synchronous_up_counter_with_load_74ls161_1_q0,
       four_bit_synchronous_up_counter_with_load_74ls161_1_q1,
       four_bit_synchronous_up_counter_with_load_74ls161_1_q2,
       four_bit_synchronous_up_counter_with_load_74ls161_1_q3;

  Four_Bit_Buffer four_bit_buffer_1 (
    .A0(four_bit_synchronous_up_counter_with_load_74ls161_1_q0),
    .A1(four_bit_synchronous_up_counter_with_load_74ls161_1_q1),
    .A2(four_bit_synchronous_up_counter_with_load_74ls161_1_q2),
    .A3(four_bit_synchronous_up_counter_with_load_74ls161_1_q3), .E(CO), .S0(BUS_OUT[0]), .S1(BUS_OUT[1]),
    .S2(BUS_OUT[2]), .S3(BUS_OUT[3]));
  Four_Bit_Synchronous_Up_Counter_with_Load_74LS161 four_bit_synchronous_up_counter_with_load_74ls161_1 (
    .Q0(four_bit_synchronous_up_counter_with_load_74ls161_1_q0),
    .Q1(four_bit_synchronous_up_counter_with_load_74ls161_1_q1),
    .Q2(four_bit_synchronous_up_counter_with_load_74ls161_1_q2),
    .Q3(four_bit_synchronous_up_counter_with_load_74ls161_1_q3), .INC(CE), .CLEAR(CLR), .CLK(CLK),
    .D0(DATA_IN[0]), .D1(DATA_IN[1]), .D2(DATA_IN[2]), .D3(DATA_IN[3]), .LOAD(J));  // open: CARRY
endmodule

// OUT
module Output_Register (
  input  [7:0] DATA_IN,
  input  CLR,
  input  OI,
  input  CLK,
  output [7:0] BUS_OUT
);

  Eight_Bit_Register eight_bit_register_1 (
    .A0(DATA_IN[0]), .A1(DATA_IN[1]), .A2(DATA_IN[2]), .A3(DATA_IN[3]), .A4(DATA_IN[4]), .A5(DATA_IN[5]),
    .A6(DATA_IN[6]), .A7(DATA_IN[7]), .CLR(CLR), .LOAD(OI), .CLK(CLK), .S0(BUS_OUT[0]), .S1(BUS_OUT[1]),
    .S2(BUS_OUT[2]), .S3(BUS_OUT[3]), .S4(BUS_OUT[4]), .S5(BUS_OUT[5]), .S6(BUS_OUT[6]), .S7(BUS_OUT[7]));
endmodule

// CONTROL
module Control_Logic_28C16 (
  input  [3:0] IR4_IR7,
  input  CF,
  input  ZF,
  input  CLK,
  input  CLR,
  output [2:0] COUNT,
  output AO,
  output AI,
  output II,
  output IO,
  output RO,
  output RI,
  output MI,
  output HLT,
  output FI,
  output J,
  output CO,
  output CE,
  output OI,
  output BI,
  output SU,
  output EO
);

  wire pull_resistor_1_node;
  wire [10:10] pull_resistor_2_node;

  Pull_Resistor #(.pull(1)) pull_resistor_1 (.node(pull_resistor_1_node));
  Four_Bit_Synchronous_Up_Counter_with_Load_74LS161 four_bit_synchronous_up_counter_with_load_74ls161_1 (
    .Q0(COUNT[0]), .Q1(COUNT[1]), .Q2(COUNT[2]), .INC(pull_resistor_1_node), .CLEAR(CLR), .CLK(CLK));  // open: Q3, CARRY, D0, D1, D2, D3, LOAD
  Pull_Resistor pull_resistor_2 (.node(pull_resistor_2_node[10]));
  ROM #(.addrWidth(11)) rom_1 (
    .addr({{2{pull_resistor_2_node[10]}}, ZF, CF, IR4_IR7, COUNT}), .data({HLT, MI, RI, RO, IO, II, AI, AO}));
  ROM #(.addrWidth(11)) rom_2 (
    .addr({{2{pull_resistor_2_node[10]}}, ZF, CF, IR4_IR7, COUNT}), .data({EO, SU, BI, OI, CE, CO, J, FI}));

  // Notes on the sheet:
  //   contents of rom_1 (hex, n*v repeats v):
  //   40 14 6*0 40 14 48 12 4*0 40 14 48 10 2 0 0 0 40 14 48 10 2 0 0 0 40 14 48 21 4*0 40 14 a 5*0 40 14
  //   8 5*0 40 14 6*0 40 14 6*0 40 14 6*0 40 14 6*0 40 14 6*0 40 14 6*0 40 14 6*0 40 14 1 5*0 40 14 80 5*0
  //   40 14 6*0 40 14 48 12 4*0 40 14 48 10 2 0 0 0 40 14 48 10 2 0 0 0 40 14 48 21 4*0 40 14 a 5*0 40 14
  //   8 5*0 40 14 8 5*0 40 14 6*0 40 14 6*0 40 14 6*0 40 14 6*0 40 14 6*0 40 14 6*0 40 14 1 5*0 40 14 80
  //   5*0 40 14 6*0 40 14 48 12 4*0 40 14 48 10 2 0 0 0 40 14 48 10 2 0 0 0 40 14 48 21 4*0 40 14 a 5*0 40
  //   14 8 5*0 40 14 6*0 40 14 8 5*0 40 14 6*0 40 14 6*0 40 14 6*0 40 14 6*0 40 14 6*0 40 14 1 5*0 40 14
  //   80 5*0 40 14 6*0 40 14 48 12 4*0 40 14 48 10 2 0 0 0 40 14 48 10 2 0 0 0 40 14 48 21 4*0 40 14 a 5*0
  //   40 14 8 5*0 40 14 8 5*0 40 14 8 5*0 40 14 6*0 40 14 6*0 40 14 6*0 40 14 6*0 40 14 6*0 40 14 1 5*0 40
  //   14 80
  //   contents of rom_2 (hex, n*v repeats v):
  //   4 8 6*0 4 8 6*0 4 8 0 20 81 0 0 0 4 8 0 20 c1 0 0 0 4 8 6*0 4 8 6*0 4 8 2 5*0 4 8 6*0 4 8 6*0 4 8
  //   6*0 4 8 6*0 4 8 6*0 4 8 6*0 4 8 6*0 4 8 10 5*0 4 8 6*0 4 8 6*0 4 8 6*0 4 8 0 20 81 0 0 0 4 8 0 20 c1
  //   0 0 0 4 8 6*0 4 8 6*0 4 8 2 5*0 4 8 2 5*0 4 8 6*0 4 8 6*0 4 8 6*0 4 8 6*0 4 8 6*0 4 8 6*0 4 8 10 5*0
  //   4 8 6*0 4 8 6*0 4 8 6*0 4 8 0 20 81 0 0 0 4 8 0 20 c1 0 0 0 4 8 6*0 4 8 6*0 4 8 2 5*0 4 8 6*0 4 8 2
  //   5*0 4 8 6*0 4 8 6*0 4 8 6*0 4 8 6*0 4 8 6*0 4 8 10 5*0 4 8 6*0 4 8 6*0 4 8 6*0 4 8 0 20 81 0 0 0 4 8
  //   0 20 c1 0 0 0 4 8 6*0 4 8 6*0 4 8 2 5*0 4 8 2 5*0 4 8 2 5*0 4 8 6*0 4 8 6*0 4 8 6*0 4 8 6*0 4 8 6*0
  //   4 8 10 5*0 4 8
endmodule

module RAM_Programmer (
  input  INC_ENABLE,
  input  RESET,
  input  STEP,
  output [3:0] ADDR,
  output [7:0] DATA
);

  Four_Bit_Synchronous_Up_Counter four_bit_synchronous_up_counter_1 (
    .INC(INC_ENABLE), .CLEAR(RESET), .CLK(STEP), .Q0(ADDR[0]), .Q1(ADDR[1]), .Q2(ADDR[2]), .Q3(ADDR[3]));  // open: CARRY
  ROM #(.addrWidth(4)) rom_1 (.addr(ADDR), .data(DATA));
endmodule

module Four_Bit_7_Seg (
  input  [3:0] BCD_IN,
  output [6:0] SEG_OUT
);

  ROM #(.addrWidth(4), .dataWidth(7)) rom_1 (.addr(BCD_IN), .data(SEG_OUT));

  // Notes on the sheet:
  //   contents of rom_1 (hex, n*v repeats v):
  //   7e 30 6d 79 33 5b 5f 70 7f 7b
endmodule

module Twelve_Bit_BCD_to_7_Segs (
  input  [7:0] BINARY_IN,
  output [3:0] BCD_0,
  output [3:0] BCD_1,
  output [3:0] BCD_2
);

  ROM #(.dataWidth(12)) rom_1 (.addr(BINARY_IN), .data({BCD_2, BCD_1, BCD_0}));

  // Notes on the sheet:
  //   contents of rom_1 (hex, n*v repeats v):
  //   0 1 2 3 4 5 6 7 8 9 10 11 12 13 14 15 16 17 18 19 20 21 22 23 24 25 26 27 28 29 30 31 32 33 34 35 36
  //   37 38 39 40 41 42 43 44 45 46 47 48 49 50 51 52 53 54 55 56 57 58 59 60 61 62 63 64 65 66 67 68 69
  //   70 71 72 73 74 75 76 77 78 79 80 81 82 83 84 85 86 87 88 89 90 91 92 93 94 95 96 97 98 99 100 101
  //   102 103 104 105 106 107 108 109 110 111 112 113 114 115 116 117 118 119 120 121 122 123 124 125 126
  //   127 128 129 130 131 132 133 134 135 136 137 138 139 140 141 142 143 144 145 146 147 148 149 150 151
  //   152 153 154 155 156 157 158 159 160 161 162 163 164 165 166 167 168 169 170 171 172 173 174 175 176
  //   177 178 179 180 181 182 183 184 185 186 187 188 189 190 191 192 193 194 195 196 197 198 199 200 201
  //   202 203 204 205 206 207 208 209 210 211 212 213 214 215 216 217 218 219 220 221 222 223 224 225 226
  //   227 228 229 230 231 232 233 234 235 236 237 238 239 240 241 242 243 244 245 246 247 248 249 250 251
  //   252 253 254 255
endmodule

module CPU (
  input  RESET,
  input  PROG_RAM,
  output [3:0] PC,
  output [7:0] A_DATA,
  output [7:0] B_DATA,
  output [3:0] MAR,
  output [7:0] BUS_DATA,
  output [3:0] IR,
  output ZF,
  output CF
);

  wire CLK_out, COMMIT_out, control_logic_28c16_1_ai, control_logic_28c16_1_ao, control_logic_28c16_1_bi,
       control_logic_28c16_1_ce, control_logic_28c16_1_co, control_logic_28c16_1_eo,
       control_logic_28c16_1_fi, control_logic_28c16_1_ii, control_logic_28c16_1_io, control_logic_28c16_1_j,
       control_logic_28c16_1_mi, control_logic_28c16_1_oi, control_logic_28c16_1_ri,
       control_logic_28c16_1_ro, control_logic_28c16_1_su, pull_resistor_1_node, STEP_out;
  wire [3:0] ram_programmer_1_addr, twelve_bit_bcd_to_7_segs_1_bcd_0, twelve_bit_bcd_to_7_segs_1_bcd_1,
       twelve_bit_bcd_to_7_segs_1_bcd_2;
  wire [6:0] four_bit_7_seg_1_seg_out, four_bit_7_seg_2_seg_out, four_bit_7_seg_3_seg_out;
  wire [7:0] output_register_1_bus_out, quad_2_to_1_mux_1_bit_74ls157_1_s0, ram_programmer_1_data;

  Clock CLK (.out(CLK_out));
  Program_Counter program_counter_1 (
    .DATA_IN(BUS_DATA[3:0]), .CO(control_logic_28c16_1_co), .J(control_logic_28c16_1_j), .CLK(CLK_out),
    .CE(control_logic_28c16_1_ce), .CLR(RESET), .BUS_OUT(BUS_DATA[3:0]));
  Four_Bit_MAR four_bit_mar_1 (
    .DATA_IN(ram_programmer_1_addr), .BUS(BUS_DATA[3:0]), .PROG(PROG_RAM), .CLR(RESET),
    .MI(control_logic_28c16_1_mi), .CLK(CLK_out), .A0_A4(MAR));
  RAM ram_1 (
    .DATA_IN(quad_2_to_1_mux_1_bit_74ls157_1_s0), .A3(MAR[3]), .A2(MAR[2]), .A1(MAR[1]), .A0(MAR[0]),
    .TOGGLE(COMMIT_out), .PROG(PROG_RAM), .CLK(CLK_out), .RI(control_logic_28c16_1_ri),
    .RO(control_logic_28c16_1_ro), .BUS_OUT(BUS_DATA));  // open: CLR
  RAM_Programmer ram_programmer_1 (
    .DATA(ram_programmer_1_data), .RESET(RESET), .INC_ENABLE(PROG_RAM), .ADDR(ram_programmer_1_addr),
    .STEP(STEP_out));
  Button COMMIT (.out(COMMIT_out));
  Button STEP (.out(STEP_out));
  Quad_2_to_1_Mux_1_Bit_74LS157 quad_2_to_1_mux_1_bit_74ls157_1 (
    .SEL(PROG_RAM), .ENABLE(pull_resistor_1_node), .B3(ram_programmer_1_data[3]), .A3(BUS_DATA[3]),
    .B2(ram_programmer_1_data[2]), .A2(BUS_DATA[2]), .B1(ram_programmer_1_data[1]), .A1(BUS_DATA[1]),
    .B0(ram_programmer_1_data[0]), .A0(BUS_DATA[0]), .S3(quad_2_to_1_mux_1_bit_74ls157_1_s0[3]),
    .S2(quad_2_to_1_mux_1_bit_74ls157_1_s0[2]), .S1(quad_2_to_1_mux_1_bit_74ls157_1_s0[1]),
    .S0(quad_2_to_1_mux_1_bit_74ls157_1_s0[0]));
  Quad_2_to_1_Mux_1_Bit_74LS157 quad_2_to_1_mux_1_bit_74ls157_2 (
    .SEL(PROG_RAM), .ENABLE(pull_resistor_1_node), .B3(ram_programmer_1_data[7]), .A3(BUS_DATA[7]),
    .B2(ram_programmer_1_data[6]), .A2(BUS_DATA[6]), .B1(ram_programmer_1_data[5]), .A1(BUS_DATA[5]),
    .B0(ram_programmer_1_data[4]), .A0(BUS_DATA[4]), .S3(quad_2_to_1_mux_1_bit_74ls157_1_s0[7]),
    .S2(quad_2_to_1_mux_1_bit_74ls157_1_s0[6]), .S1(quad_2_to_1_mux_1_bit_74ls157_1_s0[5]),
    .S0(quad_2_to_1_mux_1_bit_74ls157_1_s0[4]));
  Pull_Resistor #(.pull(1)) pull_resistor_1 (.node(pull_resistor_1_node));
  A_B_Reg A (
    .BUS(BUS_DATA), .DATA_IN(BUS_DATA), .CLK(CLK_out), .AI(control_logic_28c16_1_ai), .CLR(RESET),
    .AO(control_logic_28c16_1_ao), .A0_A7(A_DATA));
  A_B_Reg B (
    .BUS(BUS_DATA), .DATA_IN(BUS_DATA), .CLK(CLK_out), .AI(control_logic_28c16_1_bi), .CLR(RESET),
    .A0_A7(B_DATA));  // open: AO
  Instruction_Reg instruction_reg_1 (
    .BUS(BUS_DATA), .DATA_IN(BUS_DATA), .CLK(CLK_out), .II(control_logic_28c16_1_ii), .CLR(RESET),
    .IO(control_logic_28c16_1_io), .IR4_IR7(IR));
  Control_Logic_28C16 control_logic_28c16_1 (
    .IR4_IR7(IR), .MI(control_logic_28c16_1_mi), .RI(control_logic_28c16_1_ri),
    .RO(control_logic_28c16_1_ro), .IO(control_logic_28c16_1_io), .II(control_logic_28c16_1_ii),
    .AI(control_logic_28c16_1_ai), .AO(control_logic_28c16_1_ao), .EO(control_logic_28c16_1_eo),
    .SU(control_logic_28c16_1_su), .BI(control_logic_28c16_1_bi), .OI(control_logic_28c16_1_oi),
    .CE(control_logic_28c16_1_ce), .CO(control_logic_28c16_1_co), .J(control_logic_28c16_1_j),
    .FI(control_logic_28c16_1_fi), .CLK(CLK_out), .CLR(RESET), .CF(CF), .ZF(ZF));  // open: COUNT, HLT
  ALU alu_1 (
    .SUB(control_logic_28c16_1_su), .A0(A_DATA[0]), .A1(A_DATA[1]), .A2(A_DATA[2]), .A3(A_DATA[3]),
    .A4(A_DATA[4]), .A5(A_DATA[5]), .A6(A_DATA[6]), .A7(A_DATA[7]), .B0(B_DATA[0]), .B1(B_DATA[1]),
    .B2(B_DATA[2]), .B3(B_DATA[3]), .B4(B_DATA[4]), .B5(B_DATA[5]), .B6(B_DATA[6]), .B7(B_DATA[7]),
    .EO(control_logic_28c16_1_eo), .FLAG_CLR(RESET), .CLK(CLK_out), .FI(control_logic_28c16_1_fi),
    .BUS(BUS_DATA), .CF(CF), .ZF(ZF));
  Output_Register output_register_1 (
    .BUS_OUT(output_register_1_bus_out), .CLK(CLK_out), .OI(control_logic_28c16_1_oi), .CLR(RESET),
    .DATA_IN(BUS_DATA));
  Twelve_Bit_BCD_to_7_Segs twelve_bit_bcd_to_7_segs_1 (
    .BCD_2(twelve_bit_bcd_to_7_segs_1_bcd_2), .BCD_1(twelve_bit_bcd_to_7_segs_1_bcd_1),
    .BCD_0(twelve_bit_bcd_to_7_segs_1_bcd_0), .BINARY_IN(output_register_1_bus_out));
  Four_Bit_7_Seg four_bit_7_seg_1 (.SEG_OUT(four_bit_7_seg_1_seg_out), .BCD_IN(twelve_bit_bcd_to_7_segs_1_bcd_2));
  Four_Bit_7_Seg four_bit_7_seg_2 (.SEG_OUT(four_bit_7_seg_2_seg_out), .BCD_IN(twelve_bit_bcd_to_7_segs_1_bcd_1));
  Four_Bit_7_Seg four_bit_7_seg_3 (.SEG_OUT(four_bit_7_seg_3_seg_out), .BCD_IN(twelve_bit_bcd_to_7_segs_1_bcd_0));
  _7_Segment_Display u_7_segment_display_1 (
    .g(four_bit_7_seg_1_seg_out[0]), .f(four_bit_7_seg_1_seg_out[1]), .a(four_bit_7_seg_1_seg_out[6]),
    .b(four_bit_7_seg_1_seg_out[5]), .e(four_bit_7_seg_1_seg_out[2]), .d(four_bit_7_seg_1_seg_out[3]),
    .c(four_bit_7_seg_1_seg_out[4]));  // open: dp
  _7_Segment_Display u_7_segment_display_2 (
    .g(four_bit_7_seg_3_seg_out[0]), .f(four_bit_7_seg_3_seg_out[1]), .a(four_bit_7_seg_3_seg_out[6]),
    .b(four_bit_7_seg_3_seg_out[5]), .e(four_bit_7_seg_3_seg_out[2]), .d(four_bit_7_seg_3_seg_out[3]),
    .c(four_bit_7_seg_3_seg_out[4]));  // open: dp
  _7_Segment_Display u_7_segment_display_3 (
    .g(four_bit_7_seg_2_seg_out[0]), .f(four_bit_7_seg_2_seg_out[1]), .a(four_bit_7_seg_2_seg_out[6]),
    .b(four_bit_7_seg_2_seg_out[5]), .e(four_bit_7_seg_2_seg_out[2]), .d(four_bit_7_seg_2_seg_out[3]),
    .c(four_bit_7_seg_2_seg_out[4]));  // open: dp

  assign PC = BUS_DATA[3:0];
endmodule
